# Fritzing sketch Virtual Piano (saved by Fritzing 0.9.2b)
breadboards: 1

parts:
  Part1 = Arduino Uno (Rev3)
  LED1 = LED - 5mm [color="Red (633nm)" package="5 mm [THT]"]
  R1 = Resistor [tolerance=±5% resistance=1k package=THT]
  LED2 = LED - 5mm [color="Green (560nm)" package="5 mm [THT]"]
  R2 = Resistor [tolerance=±5% resistance=1k package=THT]
  Part2 = SRF05 Ultrasonic Rangefinder
  J1 = Piezo Speaker
  R3 = Resistor [tolerance=±5% resistance=100 package=THT]

nets:
  N1: Part1.D8, J1.pin2
  N2: Part1.D10_PWM/SS, LED2.anode
  N3: Part1.D11_PWM/MOSI, LED1.anode
  N4: Part1.D12/MISO, Part2.Echo
  N5: Part1.D13/SCK, Part2.Trig
  5V: Part1.5V, Part2.VCC
  GND: Part1.GND, R1.Pin_1, R2.Pin_1, Part2.GND, R3.Pin_1
  N6: LED1.cathode, R1.Pin_0
  N7: LED2.cathode, R2.Pin_0
  N8: J1.pin1, R3.Pin_0
